// Logisim project 19101284.circ as structural Verilog: 16 circuits, main circuit main
module main (
  input  Ach
);

  wire button_1_out, button_2_out, ChSelector_out, clock_1_out, MonitorSelector_out;
  wire [1:0] twobitcounter_1_d, twobitcounter_2_d;
  wire [9:0] volumecontroller_1_out_5, volumecontroller_1_out_6, volumecontroller_1_out_7,
       volumecontroller_1_out_8;
  wire [15:0] multiplexer_3_out, multiplexer_3_out_2, multiplexer_3_out_3, multiplexer_3_out_4,
       multiplexer_4_out, multiplexer_4_out_2, multiplexer_4_out_3, multiplexer_4_out_4, multiplexer_8_out,
       multiplexer_8_out_2, multiplexer_8_out_3, multiplexer_8_out_4, multiplexer_11_out,
       multiplexer_11_out_2, multiplexer_11_out_3, multiplexer_11_out_4, multiplexer_12_out,
       multiplexer_12_out_2, multiplexer_12_out_3, multiplexer_12_out_4, multiplexer_15_out,
       multiplexer_15_out_2, multiplexer_15_out_3, multiplexer_15_out_4, multiplexer_16_out,
       multiplexer_16_out_2, multiplexer_16_out_3, multiplexer_16_out_4;
  wire [63:0] channelcontroller_1_l1, channelcontroller_1_l2, channelcontroller_1_l3, channelcontroller_1_l4,
       demultiplexer_1_out0, demultiplexer_1_out1, demultiplexer_1_out2, demultiplexer_1_out3,
       demultiplexer_2_out0, demultiplexer_2_out1, demultiplexer_2_out2, demultiplexer_2_out3,
       demultiplexer_3_out0, demultiplexer_3_out1, demultiplexer_3_out2, demultiplexer_3_out3,
       demultiplexer_4_out0, demultiplexer_4_out1, demultiplexer_4_out2, demultiplexer_4_out3,
       multiplexer_1_out, multiplexer_2_out, multiplexer_5_out, multiplexer_6_out, multiplexer_7_out,
       multiplexer_9_out, multiplexer_10_out, multiplexer_13_out, multiplexer_14_out;

  Clock clock_1 (.out(clock_1_out));
  ChannelController channelcontroller_1 (
    .CLK(clock_1_out), .in_2(twobitcounter_2_d), .L1(channelcontroller_1_l1), .L2(channelcontroller_1_l2),
    .L3(channelcontroller_1_l3), .L4(channelcontroller_1_l4));
  Demultiplexer #(.select(2), .width(64)) demultiplexer_1 (
    .out0(demultiplexer_1_out0), .out1(demultiplexer_1_out1), .out2(demultiplexer_1_out2),
    .out3(demultiplexer_1_out3), .in(channelcontroller_1_l1), .sel(twobitcounter_1_d));
  Demultiplexer #(.select(2), .width(64)) demultiplexer_2 (
    .out0(demultiplexer_2_out0), .out1(demultiplexer_2_out1), .out2(demultiplexer_2_out2),
    .out3(demultiplexer_2_out3), .in(channelcontroller_1_l2), .sel(twobitcounter_1_d));
  Demultiplexer #(.select(2), .width(64)) demultiplexer_3 (
    .out0(demultiplexer_3_out0), .out1(demultiplexer_3_out1), .out2(demultiplexer_3_out2),
    .out3(demultiplexer_3_out3), .in(channelcontroller_1_l3), .sel(twobitcounter_1_d));
  Demultiplexer #(.select(2), .width(64)) demultiplexer_4 (
    .out0(demultiplexer_4_out0), .out1(demultiplexer_4_out1), .out2(demultiplexer_4_out2),
    .out3(demultiplexer_4_out3), .in(channelcontroller_1_l4), .sel(twobitcounter_1_d));
  Multiplexer #(.width(64)) multiplexer_1 (
    .in0(demultiplexer_1_out3), .in1(channelcontroller_1_l1), .out(multiplexer_1_out), .sel(Ach));
  DotMatrix #(.matrixcols(16), .matrixrows(16)) dotmatrix_1 (
    .col0(multiplexer_1_out[63:48]), .col1(multiplexer_1_out[47:32]), .col2(multiplexer_1_out[31:16]),
    .col3(multiplexer_1_out[15:0]), .col4(multiplexer_2_out[63:48]), .col5(multiplexer_2_out[47:32]),
    .col6(multiplexer_2_out[31:16]), .col7(multiplexer_2_out[15:0]), .col8(multiplexer_3_out_4),
    .col9(multiplexer_3_out_3), .col10(multiplexer_3_out_2), .col11(multiplexer_3_out),
    .col12(multiplexer_4_out_4), .col13(multiplexer_4_out_3), .col14(multiplexer_4_out_2),
    .col15(multiplexer_4_out));
  Multiplexer #(.width(64)) multiplexer_2 (
    .in0(demultiplexer_2_out3), .in1(channelcontroller_1_l2), .out(multiplexer_2_out), .sel(Ach));
  Multiplexer #(.width(64)) multiplexer_3 (
    .in0(demultiplexer_3_out3), .in1(channelcontroller_1_l3),
    .out({multiplexer_3_out_4, multiplexer_3_out_3, multiplexer_3_out_2, multiplexer_3_out}), .sel(Ach));
  DotMatrix #(.matrixcols(2), .matrixrows(10)) dotmatrix_2 (
    .col0(volumecontroller_1_out_8), .col1(volumecontroller_1_out_8));
  TwoBitCounter twobitcounter_1 (.CLK(MonitorSelector_out), .D(twobitcounter_1_d));
  Button MonitorSelector (.out(MonitorSelector_out));
  TwoBitCounter twobitcounter_2 (.CLK(ChSelector_out), .D(twobitcounter_2_d));
  Button ChSelector (.out(ChSelector_out));
  Hex_Digit_Display #(.decimalPoint("false")) Monitor (.value({2'b00, twobitcounter_1_d}));
  Multiplexer #(.width(64)) multiplexer_4 (
    .in0(demultiplexer_4_out3), .in1(channelcontroller_1_l4),
    .out({multiplexer_4_out_4, multiplexer_4_out_3, multiplexer_4_out_2, multiplexer_4_out}), .sel(Ach));
  Hex_Digit_Display #(.decimalPoint("false")) Ch (.value({2'b00, twobitcounter_2_d}));
  Multiplexer #(.width(64)) multiplexer_5 (
    .in0(demultiplexer_1_out2), .in1(channelcontroller_1_l1), .out(multiplexer_5_out), .sel(Ach));
  Multiplexer #(.width(64)) multiplexer_6 (
    .in0(demultiplexer_2_out2), .in1(channelcontroller_1_l2), .out(multiplexer_6_out), .sel(Ach));
  DotMatrix #(.matrixcols(16), .matrixrows(16)) dotmatrix_3 (
    .col0(multiplexer_5_out[63:48]), .col1(multiplexer_5_out[47:32]), .col2(multiplexer_5_out[31:16]),
    .col3(multiplexer_5_out[15:0]), .col4(multiplexer_6_out[63:48]), .col5(multiplexer_6_out[47:32]),
    .col6(multiplexer_6_out[31:16]), .col7(multiplexer_6_out[15:0]), .col8(multiplexer_7_out[63:48]),
    .col9(multiplexer_7_out[47:32]), .col10(multiplexer_7_out[31:16]), .col11(multiplexer_7_out[15:0]),
    .col12(multiplexer_8_out_4), .col13(multiplexer_8_out_3), .col14(multiplexer_8_out_2),
    .col15(multiplexer_8_out));
  Button button_1 (.out(button_1_out));
  Button button_2 (.out(button_2_out));
  Multiplexer #(.width(64)) multiplexer_7 (
    .in0(demultiplexer_3_out2), .in1(channelcontroller_1_l3), .out(multiplexer_7_out), .sel(Ach));
  Multiplexer #(.width(64)) multiplexer_8 (
    .in0(demultiplexer_4_out2), .in1(channelcontroller_1_l4),
    .out({multiplexer_8_out_4, multiplexer_8_out_3, multiplexer_8_out_2, multiplexer_8_out}), .sel(Ach));
  DotMatrix #(.matrixcols(2), .matrixrows(10)) dotmatrix_4 (
    .col0(volumecontroller_1_out_7), .col1(volumecontroller_1_out_7));
  Multiplexer #(.width(64)) multiplexer_9 (
    .in0(demultiplexer_1_out1), .in1(channelcontroller_1_l1), .out(multiplexer_9_out), .sel(Ach));
  Multiplexer #(.width(64)) multiplexer_10 (
    .in0(demultiplexer_2_out1), .in1(channelcontroller_1_l2), .out(multiplexer_10_out), .sel(Ach));
  DotMatrix #(.matrixcols(16), .matrixrows(16)) dotmatrix_5 (
    .col0(multiplexer_9_out[63:48]), .col1(multiplexer_9_out[47:32]), .col2(multiplexer_9_out[31:16]),
    .col3(multiplexer_9_out[15:0]), .col4(multiplexer_10_out[63:48]), .col5(multiplexer_10_out[47:32]),
    .col6(multiplexer_10_out[31:16]), .col7(multiplexer_10_out[15:0]), .col8(multiplexer_11_out_4),
    .col9(multiplexer_11_out_3), .col10(multiplexer_11_out_2), .col11(multiplexer_11_out),
    .col12(multiplexer_12_out_4), .col13(multiplexer_12_out_3), .col14(multiplexer_12_out_2),
    .col15(multiplexer_12_out));
  VolumeController volumecontroller_1 (
    .Up(button_1_out), .Down(button_2_out), .ch(twobitcounter_1_d), .Ach(Ach),
    .out_5(volumecontroller_1_out_5), .out_6(volumecontroller_1_out_6), .out_7(volumecontroller_1_out_7),
    .out_8(volumecontroller_1_out_8));
  Multiplexer #(.width(64)) multiplexer_11 (
    .in0(demultiplexer_3_out1), .in1(channelcontroller_1_l3),
    .out({multiplexer_11_out_4, multiplexer_11_out_3, multiplexer_11_out_2, multiplexer_11_out}), .sel(Ach));
  Multiplexer #(.width(64)) multiplexer_12 (
    .in0(demultiplexer_4_out1), .in1(channelcontroller_1_l4),
    .out({multiplexer_12_out_4, multiplexer_12_out_3, multiplexer_12_out_2, multiplexer_12_out}), .sel(Ach));
  DotMatrix #(.matrixcols(2), .matrixrows(10)) dotmatrix_6 (
    .col0(volumecontroller_1_out_6), .col1(volumecontroller_1_out_6));
  Multiplexer #(.width(64)) multiplexer_13 (
    .in0(demultiplexer_1_out0), .in1(channelcontroller_1_l1), .out(multiplexer_13_out), .sel(Ach));
  Multiplexer #(.width(64)) multiplexer_14 (
    .in0(demultiplexer_2_out0), .in1(channelcontroller_1_l2), .out(multiplexer_14_out), .sel(Ach));
  DotMatrix #(.matrixcols(16), .matrixrows(16)) dotmatrix_7 (
    .col0(multiplexer_13_out[63:48]), .col1(multiplexer_13_out[47:32]), .col2(multiplexer_13_out[31:16]),
    .col3(multiplexer_13_out[15:0]), .col4(multiplexer_14_out[63:48]), .col5(multiplexer_14_out[47:32]),
    .col6(multiplexer_14_out[31:16]), .col7(multiplexer_14_out[15:0]), .col8(multiplexer_15_out_4),
    .col9(multiplexer_15_out_3), .col10(multiplexer_15_out_2), .col11(multiplexer_15_out),
    .col12(multiplexer_16_out_4), .col13(multiplexer_16_out_3), .col14(multiplexer_16_out_2),
    .col15(multiplexer_16_out));
  Multiplexer #(.width(64)) multiplexer_15 (
    .in0(demultiplexer_3_out0), .in1(channelcontroller_1_l3),
    .out({multiplexer_15_out_4, multiplexer_15_out_3, multiplexer_15_out_2, multiplexer_15_out}), .sel(Ach));
  Multiplexer #(.width(64)) multiplexer_16 (
    .in0(demultiplexer_4_out0), .in1(channelcontroller_1_l4),
    .out({multiplexer_16_out_4, multiplexer_16_out_3, multiplexer_16_out_2, multiplexer_16_out}), .sel(Ach));
  DotMatrix #(.matrixcols(2), .matrixrows(10)) dotmatrix_8 (
    .col0(volumecontroller_1_out_5), .col1(volumecontroller_1_out_5));
endmodule

module HalfAdder (
  input  A,
  input  B,
  output S,
  output C
);

  xor xor_1 (S, A, B);
  and and_1 (C, A, B);
endmodule

module FullAdder (
  input  A,
  input  B,
  input  C_in,
  output S,
  output C_out
);

  wire halfadder_1_c, halfadder_1_s, halfadder_2_c;

  HalfAdder halfadder_1 (.A(A), .B(B), .S(halfadder_1_s), .C(halfadder_1_c));
  HalfAdder halfadder_2 (.A(halfadder_1_s), .B(C_in), .S(S), .C(halfadder_2_c));
  or or_1 (C_out, halfadder_1_c, halfadder_2_c);
endmodule

module MyCounter (
  input  CLK,
  output [7:0] D
);

  wire and_1_out, and_2_out, and_3_out, and_4_out, and_5_out, and_6_out;

  J_K_Flip_Flop j_k_ff_1 (.J(1'b1), .K(1'b1), .clk(CLK), .Q(D[0]));  // open: Qn, preset, reset
  J_K_Flip_Flop j_k_ff_2 (.J(D[0]), .K(D[0]), .clk(CLK), .Q(D[1]));  // open: Qn, preset, reset
  and and_1 (and_1_out, D[0], D[1]);
  J_K_Flip_Flop j_k_ff_3 (.J(and_1_out), .K(and_1_out), .clk(CLK), .Q(D[2]));  // open: Qn, preset, reset
  and and_2 (and_2_out, and_1_out, D[2]);
  J_K_Flip_Flop j_k_ff_4 (.J(and_2_out), .K(and_2_out), .clk(CLK), .Q(D[3]));  // open: Qn, preset, reset
  and and_3 (and_3_out, and_2_out, D[3]);
  J_K_Flip_Flop j_k_ff_5 (.J(and_3_out), .K(and_3_out), .clk(CLK), .Q(D[4]));  // open: Qn, preset, reset
  and and_4 (and_4_out, and_3_out, D[4]);
  J_K_Flip_Flop j_k_ff_6 (.J(and_4_out), .K(and_4_out), .clk(CLK), .Q(D[5]));  // open: Qn, preset, reset
  and and_5 (and_5_out, and_4_out, D[5]);
  J_K_Flip_Flop j_k_ff_7 (.J(and_5_out), .K(and_5_out), .clk(CLK), .Q(D[6]));  // open: Qn, preset, reset
  and and_6 (and_6_out, and_5_out, D[6]);
  J_K_Flip_Flop j_k_ff_8 (.J(and_6_out), .K(and_6_out), .clk(CLK), .Q(D[7]));  // open: Qn, preset, reset
endmodule

module EightBitAdder (
  input  [7:0] A,
  input  [7:0] B,
  output [7:0] S,
  output OVR
);

  wire fulladder_1_c_out, fulladder_2_c_out, fulladder_3_c_out, fulladder_4_c_out, fulladder_5_c_out,
       fulladder_6_c_out, fulladder_7_c_out;

  FullAdder fulladder_1 (.A(A[0]), .B(B[0]), .C_in(1'b0), .S(S[0]), .C_out(fulladder_1_c_out));
  FullAdder fulladder_2 (.A(A[1]), .B(B[1]), .C_in(fulladder_1_c_out), .S(S[1]), .C_out(fulladder_2_c_out));
  FullAdder fulladder_3 (.A(A[2]), .B(B[2]), .C_in(fulladder_2_c_out), .S(S[2]), .C_out(fulladder_3_c_out));
  FullAdder fulladder_4 (.A(A[3]), .B(B[3]), .C_in(fulladder_3_c_out), .S(S[3]), .C_out(fulladder_4_c_out));
  FullAdder fulladder_5 (.A(A[4]), .B(B[4]), .C_in(fulladder_4_c_out), .S(S[4]), .C_out(fulladder_5_c_out));
  FullAdder fulladder_6 (.A(A[5]), .B(B[5]), .C_in(fulladder_5_c_out), .S(S[5]), .C_out(fulladder_6_c_out));
  FullAdder fulladder_7 (.A(A[6]), .B(B[6]), .C_in(fulladder_6_c_out), .S(S[6]), .C_out(fulladder_7_c_out));
  FullAdder fulladder_8 (.A(A[7]), .B(B[7]), .C_in(fulladder_7_c_out), .S(S[7]), .C_out(OVR));
endmodule

module OneOfTwoDecoder (
  input  A,
  input  B,
  output Y0,
  output Y1,
  output Y2,
  output Y3
);

  wire not_1_out, not_2_out;

  not not_1 (not_1_out, A);
  not not_2 (not_2_out, B);
  and and_1 (Y0, not_1_out, not_2_out);
  and and_2 (Y1, A, not_2_out);
  and and_3 (Y2, not_1_out, B);
  and and_4 (Y3, A, B);

  // Notes on the sheet:
  //   OneOfTwoDecoder: Not
endmodule

module TwoBitCounter (
  input  CLK,
  output [1:0] D
);

  J_K_Flip_Flop j_k_ff_1 (.J(1'b1), .K(1'b1), .clk(CLK), .Q(D[0]));  // open: Qn, preset, reset
  J_K_Flip_Flop j_k_ff_2 (.J(D[0]), .K(D[0]), .clk(CLK), .Q(D[1]));  // open: Qn, preset, reset
endmodule

module LedMatrixSimulator (
  input  [7:0] in_1,
  input  [7:0] in_2,
  input  [7:0] in_3,
  input  [7:0] in_4,
  input  [7:0] in_5,
  input  [7:0] in_6,
  input  [7:0] in_7,
  input  [7:0] in_8,
  input  [7:0] in_9,
  input  [7:0] in_10,
  input  [7:0] in_11,
  input  [7:0] in_12,
  input  [7:0] in_13,
  input  [7:0] in_14,
  input  [7:0] in_15,
  input  [7:0] in_16,
  input  [7:0] in_17,
  input  [7:0] in_18,
  input  [7:0] in_19,
  input  [7:0] in_20,
  input  [7:0] in_21,
  input  [7:0] in_22,
  input  [7:0] in_23,
  input  [7:0] in_24,
  input  [7:0] in_25,
  input  [7:0] in_26,
  input  [7:0] in_27,
  input  [7:0] in_28,
  input  [7:0] in_29,
  input  [7:0] in_30,
  input  [7:0] in_31,
  input  [7:0] in_32,
  output [63:0] out_33,
  output [63:0] out_34,
  output [63:0] out_35,
  output [63:0] out_36
);

  DotMatrix #(.matrixcols(16), .matrixrows(16)) dotmatrix_1 (
    .col0({in_1, in_17}), .col1({in_2, in_18}), .col2({in_3, in_19}), .col3({in_4, in_20}),
    .col4({in_5, in_21}), .col5({in_6, in_22}), .col6({in_7, in_23}), .col7({in_8, in_24}),
    .col8({in_9, in_25}), .col9({in_10, in_26}), .col10({in_11, in_27}), .col11({in_12, in_28}),
    .col12({in_13, in_29}), .col13({in_14, in_30}), .col14({in_15, in_31}), .col15({in_16, in_32}));
  DotMatrix #(.matrixcols(16), .matrixrows(16)) dotmatrix_2 (
    .col0({16{1'b0}}), .col1(16'h80), .col2(16'h1080), .col3(16'h31c1), .col4(16'h6143), .col5(16'h4d7c),
    .col6(16'h4fc0), .col7(16'h4843), .col8(16'h581c), .col9(16'h1c70), .col10(16'h6480), .col11(16'h40c0),
    .col12(16'h603c), .col13(16'h1c03), .col14(16'h3e0), .col15(16'h3e));

  assign out_33 = {in_1, in_17, in_2, in_18, in_3, in_19, in_4, in_20};
  assign out_34 = {in_13, in_29, in_14, in_30, in_15, in_31, in_16, in_32};
  assign out_35 = {in_5, in_21, in_6, in_22, in_7, in_23, in_8, in_24};
  assign out_36 = {in_9, in_25, in_10, in_26, in_11, in_27, in_12, in_28};
endmodule

module ChannelController (
  input  CLK,
  input  [1:0] in_2,
  output [63:0] L1,
  output [63:0] L2,
  output [63:0] L3,
  output [63:0] L4
);

  wire [63:0] channelanimation_1_out_18, channelanimation_1_out_19, channelanimation_1_out_20,
       channelanimation_1_out_21, channelanimation_2_out_18, channelanimation_2_out_19,
       channelanimation_2_out_20, channelanimation_2_out_21;

  ChannelAnimation channelanimation_1 (
    .in_1(64'h1cf01cf0000000), .in_2(64'h78007800000003c), .in_3(64'h3c7c007c000000),
    .in_4(64'h1c001c3f003f), .in_5(64'h38f838f8000000), .in_6(64'hf000f000000001e),
    .in_7(64'h1ef800f8000000), .in_8(64'he000e7e007e), .in_9(64'h707c707c000000),
    .in_10(64'h1e001e000000000f), .in_11(64'hff000f0000000), .in_12(64'h70007fc00fc),
    .in_13(64'he03ee03e000000), .in_14(64'h3c003c0000000007), .in_15(64'h7e000e0000000),
    .in_16(64'h38003f801f8), .CLK(CLK), .out_18(channelanimation_1_out_18),
    .out_19(channelanimation_1_out_19), .out_20(channelanimation_1_out_20), .out_21(channelanimation_1_out_21));
  Multiplexer #(.select(2), .width(64)) multiplexer_1 (
    .in0(channelanimation_1_out_18), .in1(64'h70009003303c2), .in2(channelanimation_2_out_18),
    .in3(64'h102710251fe7002), .out(L1), .sel(in_2));
  Multiplexer #(.select(2), .width(64)) multiplexer_2 (
    .in0(channelanimation_1_out_19), .in1(64'hc34080810181024), .in2(channelanimation_2_out_19),
    .in3(64'h23ffe20022002), .out(L2), .sel(in_2));
  Multiplexer #(.select(2), .width(64)) multiplexer_3 (
    .in0(channelanimation_1_out_20), .in1(64'h1044108831084a10), .in2(channelanimation_2_out_20),
    .in3(64'h3ffe010401040ffc), .out(L3), .sel(in_2));
  Multiplexer #(.select(2), .width(64)) multiplexer_4 (
    .in0(channelanimation_1_out_21), .in1(64'h4c609b80a000c000), .in2(channelanimation_2_out_21),
    .in3(64'h41ffc10041004), .out(L4), .sel(in_2));
  DotMatrix #(.matrixcols(16), .matrixrows(16)) dotmatrix_1 (
    .col0(L1[63:48]), .col1(L1[47:32]), .col2(L1[31:16]), .col3(L1[15:0]), .col4(L2[63:48]),
    .col5(L2[47:32]), .col6(L2[31:16]), .col7(L2[15:0]), .col8(L3[63:48]), .col9(L3[47:32]),
    .col10(L3[31:16]), .col11(L3[15:0]), .col12(L4[63:48]), .col13(L4[47:32]), .col14(L4[31:16]),
    .col15(L4[15:0]));
  ChannelAnimation channelanimation_2 (
    .in_1(64'h2080208061c04143), .in_2(64'h404e403040600f83), .in_3(64'h103c20e049008880),
    .in_4(64'hc87838070fc0083e), .in_5(64'h2080208061c3), .in_6(64'h414e40704fc04803),
    .in_7(64'h183c28e049008880), .in_8(64'hc87830070fc0003e), .in_9(64'h20802081),
    .in_10(64'h69c749784fc04843), .in_11(64'h583c18e069008080), .in_12(64'he078180707e0001f),
    .in_13(64'h80108031c1), .in_14(64'h61434d7c4fc04843), .in_15(64'h581c1c70648040c0),
    .in_16(64'h603c1c0303e0003e), .CLK(CLK), .out_18(channelanimation_2_out_18),
    .out_19(channelanimation_2_out_19), .out_20(channelanimation_2_out_20), .out_21(channelanimation_2_out_21));
endmodule

module BusDriver (
  input  [63:0] D3,
  input  [63:0] D2,
  input  [63:0] D1,
  input  [63:0] D0,
  input  [63:0] C3,
  input  [63:0] C2,
  input  [63:0] C1,
  input  [63:0] C0,
  input  [63:0] B3,
  input  [63:0] B2,
  input  [63:0] B1,
  input  [63:0] B0,
  input  [63:0] A3,
  input  [63:0] A2,
  input  [63:0] A1,
  input  [63:0] A0,
  input  S0,
  input  S1,
  output [63:0] L1,
  output [63:0] L2,
  output [63:0] L3,
  output [63:0] L4
);

  wire oneoftwodecoder_1_y0, oneoftwodecoder_1_y1, oneoftwodecoder_1_y2, oneoftwodecoder_1_y3;

  OneOfTwoDecoder oneoftwodecoder_1 (
    .A(S0), .B(S1), .Y0(oneoftwodecoder_1_y0), .Y1(oneoftwodecoder_1_y1), .Y2(oneoftwodecoder_1_y2),
    .Y3(oneoftwodecoder_1_y3));
  assign L1 = oneoftwodecoder_1_y3 ? D3 : 64'bz;  // Controlled_Buffer controlled_buffer_1
  assign L1 = oneoftwodecoder_1_y0 ? A3 : 64'bz;  // Controlled_Buffer controlled_buffer_2
  assign L1 = oneoftwodecoder_1_y1 ? B3 : 64'bz;  // Controlled_Buffer controlled_buffer_3
  assign L1 = oneoftwodecoder_1_y2 ? C3 : 64'bz;  // Controlled_Buffer controlled_buffer_4
  assign L2 = oneoftwodecoder_1_y3 ? D2 : 64'bz;  // Controlled_Buffer controlled_buffer_5
  assign L2 = oneoftwodecoder_1_y0 ? A2 : 64'bz;  // Controlled_Buffer controlled_buffer_6
  assign L2 = oneoftwodecoder_1_y1 ? B2 : 64'bz;  // Controlled_Buffer controlled_buffer_7
  assign L2 = oneoftwodecoder_1_y2 ? C2 : 64'bz;  // Controlled_Buffer controlled_buffer_8
  assign L3 = oneoftwodecoder_1_y3 ? D1 : 64'bz;  // Controlled_Buffer controlled_buffer_9
  assign L3 = oneoftwodecoder_1_y0 ? A1 : 64'bz;  // Controlled_Buffer controlled_buffer_10
  assign L3 = oneoftwodecoder_1_y1 ? B1 : 64'bz;  // Controlled_Buffer controlled_buffer_11
  assign L3 = oneoftwodecoder_1_y2 ? C1 : 64'bz;  // Controlled_Buffer controlled_buffer_12
  assign L4 = oneoftwodecoder_1_y3 ? D0 : 64'bz;  // Controlled_Buffer controlled_buffer_13
  assign L4 = oneoftwodecoder_1_y0 ? A0 : 64'bz;  // Controlled_Buffer controlled_buffer_14
  assign L4 = oneoftwodecoder_1_y1 ? B0 : 64'bz;  // Controlled_Buffer controlled_buffer_15
  assign L4 = oneoftwodecoder_1_y2 ? C0 : 64'bz;  // Controlled_Buffer controlled_buffer_16
endmodule

module VolumeController (
  input  Up,
  input  Down,
  input  [1:0] ch,
  input  Ach,
  output [9:0] out_5,
  output [9:0] out_6,
  output [9:0] out_7,
  output [9:0] out_8
);

  wire demultiplexer_1_out0, demultiplexer_1_out1, demultiplexer_1_out2, demultiplexer_1_out3,
       demultiplexer_2_out0, demultiplexer_2_out1, demultiplexer_2_out2, demultiplexer_2_out3,
       multiplexer_1_out, multiplexer_2_out, multiplexer_3_out, multiplexer_4_out, multiplexer_5_out,
       multiplexer_6_out, multiplexer_7_out, multiplexer_8_out;

  Demultiplexer #(.select(2)) demultiplexer_1 (
    .out0(demultiplexer_1_out0), .out1(demultiplexer_1_out1), .out2(demultiplexer_1_out2),
    .out3(demultiplexer_1_out3), .in(Up), .sel(ch));
  Demultiplexer #(.select(2)) demultiplexer_2 (
    .out0(demultiplexer_2_out0), .out1(demultiplexer_2_out1), .out2(demultiplexer_2_out2),
    .out3(demultiplexer_2_out3), .in(Down), .sel(ch));
  Multiplexer multiplexer_1 (.in0(demultiplexer_1_out0), .in1(Up), .out(multiplexer_1_out), .sel(Ach));
  Multiplexer multiplexer_2 (.in0(demultiplexer_2_out0), .in1(Down), .out(multiplexer_2_out), .sel(Ach));
  Multiplexer multiplexer_3 (.in0(demultiplexer_1_out1), .in1(Up), .out(multiplexer_3_out), .sel(Ach));
  Multiplexer multiplexer_4 (.in0(demultiplexer_2_out1), .in1(Down), .out(multiplexer_4_out), .sel(Ach));
  Multiplexer multiplexer_5 (.in0(demultiplexer_1_out2), .in1(Up), .out(multiplexer_5_out), .sel(Ach));
  Multiplexer multiplexer_6 (.in0(demultiplexer_2_out2), .in1(Down), .out(multiplexer_6_out), .sel(Ach));
  Multiplexer multiplexer_7 (.in0(demultiplexer_1_out3), .in1(Up), .out(multiplexer_7_out), .sel(Ach));
  Multiplexer multiplexer_8 (.in0(demultiplexer_2_out3), .in1(Down), .out(multiplexer_8_out), .sel(Ach));
  Volume volume_1 (.Up(multiplexer_1_out), .Down(multiplexer_2_out), .out_3(out_5));
  Volume volume_2 (.Up(multiplexer_3_out), .Down(multiplexer_4_out), .out_3(out_6));
  Volume volume_3 (.Up(multiplexer_5_out), .Down(multiplexer_6_out), .out_3(out_7));
  Volume volume_4 (.Up(multiplexer_7_out), .Down(multiplexer_8_out), .out_3(out_8));
  DotMatrix #(.matrixcols(2), .matrixrows(10)) dotmatrix_1 (.col0(out_5), .col1(out_5));
  DotMatrix #(.matrixcols(2), .matrixrows(10)) dotmatrix_2 (.col0(out_6), .col1(out_6));
  DotMatrix #(.matrixcols(2), .matrixrows(10)) dotmatrix_3 (.col0(out_7), .col1(out_7));
  DotMatrix #(.matrixcols(2), .matrixrows(10)) dotmatrix_4 (.col0(out_8), .col1(out_8));
endmodule

module BCDCounter (
  input  in_1,
  output [9:0] out_2,
  output [7:0] out_3
);

  wire and_1_out;
  wire [3:0] j_k_ff_1_q;

  J_K_Flip_Flop #(.trigger("falling")) j_k_ff_1 (
    .J(1'b1), .K(1'b1), .clk(in_1), .Q(j_k_ff_1_q[0]), .reset(and_1_out));  // open: Qn, preset
  J_K_Flip_Flop #(.trigger("falling")) j_k_ff_2 (
    .J(1'b1), .K(1'b1), .clk(j_k_ff_1_q[0]), .Q(j_k_ff_1_q[1]), .reset(and_1_out));  // open: Qn, preset
  J_K_Flip_Flop #(.trigger("falling")) j_k_ff_3 (
    .J(1'b1), .K(1'b1), .clk(j_k_ff_1_q[1]), .Q(j_k_ff_1_q[2]), .reset(and_1_out));  // open: Qn, preset
  J_K_Flip_Flop #(.trigger("falling")) j_k_ff_4 (
    .J(1'b1), .K(1'b1), .clk(j_k_ff_1_q[2]), .Q(j_k_ff_1_q[3]), .reset(and_1_out));  // open: Qn, preset
  Hex_Digit_Display hex_digit_display_1 (.value(j_k_ff_1_q));  // open: dp
  and and_1 (and_1_out, j_k_ff_1_q[1], j_k_ff_1_q[3]);
  Shifter #(.shift("rl"), .width(10)) shifter_1 (.in(10'h1), .\dist (j_k_ff_1_q), .out(out_2));
  BitAdder #(.width(10)) bitadder_1 (.in0(out_2));  // open: in1, out

  assign out_3 = out_2[7:0];
endmodule

module StoSRegister (
  input  \bit ,
  input  Clock,
  output [9:0] Up,
  output [9:0] Down
);

  D_Flip_Flop d_ff_1 (.D(\bit ), .clk(Clock), .Q(Down[9]));  // open: Qn, preset, reset
  D_Flip_Flop d_ff_2 (.D(Down[9]), .clk(Clock), .Q(Down[8]));  // open: Qn, preset, reset
  D_Flip_Flop d_ff_3 (.D(Down[8]), .clk(Clock), .Q(Down[7]));  // open: Qn, preset, reset
  D_Flip_Flop d_ff_4 (.D(Down[7]), .clk(Clock), .Q(Down[6]));  // open: Qn, preset, reset
  D_Flip_Flop d_ff_5 (.D(Down[6]), .clk(Clock), .Q(Down[5]));  // open: Qn, preset, reset
  D_Flip_Flop d_ff_6 (.D(Down[5]), .clk(Clock), .Q(Down[4]));  // open: Qn, preset, reset
  D_Flip_Flop d_ff_7 (.D(Down[4]), .clk(Clock), .Q(Down[3]));  // open: Qn, preset, reset
  D_Flip_Flop d_ff_8 (.D(Down[3]), .clk(Clock), .Q(Down[2]));  // open: Qn, preset, reset
  D_Flip_Flop d_ff_9 (.D(Down[2]), .clk(Clock), .Q(Down[1]));  // open: Qn, preset, reset
  D_Flip_Flop d_ff_10 (.D(Down[1]), .clk(Clock), .Q(Down[0]));  // open: Qn, preset, reset

  assign Up = {Down[0], Down[1], Down[2], Down[3], Down[4], Down[5], Down[6], Down[7], Down[8], Down[9]};
endmodule

module BiShiftRegister (
  input  CLK,
  input  RL,
  output [9:0] out_3
);

  wire multiplexer_1_out, multiplexer_2_out, multiplexer_3_out, multiplexer_4_out, multiplexer_5_out,
       multiplexer_6_out, multiplexer_7_out, multiplexer_8_out, multiplexer_9_out, multiplexer_10_out;

  Multiplexer multiplexer_1 (.in0(out_3[8]), .in1(1'b0), .out(multiplexer_1_out), .sel(RL));
  D_Flip_Flop d_ff_1 (.D(multiplexer_1_out), .clk(CLK), .Q(out_3[9]));  // open: Qn, preset, reset
  Multiplexer multiplexer_2 (.in0(out_3[7]), .in1(out_3[9]), .out(multiplexer_2_out), .sel(RL));
  D_Flip_Flop d_ff_2 (.D(multiplexer_2_out), .clk(CLK), .Q(out_3[8]));  // open: Qn, preset, reset
  Multiplexer multiplexer_3 (.in0(out_3[6]), .in1(out_3[8]), .out(multiplexer_3_out), .sel(RL));
  D_Flip_Flop d_ff_3 (.D(multiplexer_3_out), .clk(CLK), .Q(out_3[7]));  // open: Qn, preset, reset
  Multiplexer multiplexer_4 (.in0(out_3[5]), .in1(out_3[7]), .out(multiplexer_4_out), .sel(RL));
  D_Flip_Flop d_ff_4 (.D(multiplexer_4_out), .clk(CLK), .Q(out_3[6]));  // open: Qn, preset, reset
  Multiplexer multiplexer_5 (.in0(out_3[4]), .in1(out_3[6]), .out(multiplexer_5_out), .sel(RL));
  D_Flip_Flop d_ff_5 (.D(multiplexer_5_out), .clk(CLK), .Q(out_3[5]));  // open: Qn, preset, reset
  Multiplexer multiplexer_6 (.in0(out_3[3]), .in1(out_3[5]), .out(multiplexer_6_out), .sel(RL));
  D_Flip_Flop d_ff_6 (.D(multiplexer_6_out), .clk(CLK), .Q(out_3[4]));  // open: Qn, preset, reset
  D_Flip_Flop d_ff_7 (.D(multiplexer_7_out), .clk(CLK), .Q(out_3[3]));  // open: Qn, preset, reset
  Multiplexer multiplexer_7 (.in0(out_3[2]), .in1(out_3[4]), .out(multiplexer_7_out), .sel(RL));
  D_Flip_Flop d_ff_8 (.D(multiplexer_8_out), .clk(CLK), .Q(out_3[2]));  // open: Qn, preset, reset
  Multiplexer multiplexer_8 (.in0(out_3[1]), .in1(out_3[3]), .out(multiplexer_8_out), .sel(RL));
  D_Flip_Flop d_ff_9 (.D(multiplexer_9_out), .clk(CLK), .Q(out_3[1]));  // open: Qn, preset, reset
  Multiplexer multiplexer_9 (.in0(out_3[0]), .in1(out_3[2]), .out(multiplexer_9_out), .sel(RL));
  D_Flip_Flop d_ff_10 (.D(multiplexer_10_out), .clk(CLK), .Q(out_3[0]));  // open: Qn, preset, reset
  Multiplexer multiplexer_10 (.in0(1'b1), .in1(out_3[1]), .out(multiplexer_10_out), .sel(RL));
endmodule

module Volume (
  input  Up,
  input  Down,
  output [9:0] out_3
);

  wire d_ff_1_q, multiplexer_1_out, not_1_out;

  not not_1 (not_1_out, d_ff_1_q);
  Multiplexer multiplexer_1 (.in0(Down), .in1(Up), .out(multiplexer_1_out), .sel(Up));
  D_Flip_Flop d_ff_1 (.D(Up), .clk(multiplexer_1_out), .Q(d_ff_1_q));  // open: Qn, preset, reset
  BiShiftRegister bishiftregister_1 (.CLK(multiplexer_1_out), .RL(not_1_out), .out_3(out_3));
  DotMatrix #(.matrixcols(2), .matrixrows(10)) dotmatrix_1 (.col0(out_3), .col1(out_3));
endmodule

module ChannelAnimation (
  input  [63:0] in_1,
  input  [63:0] in_2,
  input  [63:0] in_3,
  input  [63:0] in_4,
  input  [63:0] in_5,
  input  [63:0] in_6,
  input  [63:0] in_7,
  input  [63:0] in_8,
  input  [63:0] in_9,
  input  [63:0] in_10,
  input  [63:0] in_11,
  input  [63:0] in_12,
  input  [63:0] in_13,
  input  [63:0] in_14,
  input  [63:0] in_15,
  input  [63:0] in_16,
  input  CLK,
  output [63:0] out_18,
  output [63:0] out_19,
  output [63:0] out_20,
  output [63:0] out_21
);

  wire [1:0] twobitcounter_1_d;

  TwoBitCounter twobitcounter_1 (.CLK(CLK), .D(twobitcounter_1_d));
  BusDriver busdriver_1 (
    .D3(in_1), .D2(in_2), .D1(in_3), .D0(in_4), .C3(in_5), .C2(in_6), .C1(in_7), .C0(in_8), .B3(in_9),
    .B2(in_10), .B1(in_11), .B0(in_12), .A3(in_13), .A2(in_14), .A1(in_15), .A0(in_16),
    .S0(twobitcounter_1_d[0]), .S1(twobitcounter_1_d[1]), .L1(out_18), .L2(out_19), .L3(out_20), .L4(out_21));
endmodule
